# Fritzing sketch GatewayElectronicStep1 (saved by Fritzing 0.9.3b)
circuit board: 8.46667cm x 5.64444cm
breadboards: 1

parts:
  U1 = Voltage Regulator - 3.3V [package="TO220 [THT]"]
  C3 = Electrolytic Capacitor [capacitance=100μF package="0807 [SMD, electrolytic]"]
  MOD-WIFI-ESP8266-DEV1 = Olimex ESP8266 DEV
  ULN1 = Darlington Driver [package=dil18]
  LED2 = smd LED [color="Red (633nm)" package="0603 [SMD]"]
  LED3 = smd LED [color="Blue (525nm)" package="1206 [SMD]"]
  LED4 = smd LED [color="Green (570nm)" package="0805 [SMD]"]
  R2 = Resistor [tolerance=±5% resistance=1k package=THT]
  R8 = Resistor [tolerance=±5% resistance=3.3k package=THT]
  R12 = Resistor [tolerance=±5% resistance=3.3k package=THT]
  R13 = Resistor [tolerance=±5% resistance=33k package="2512 [SMD]"]
  R14 = 2.7k Ω Resistor [package=THT]
  Composant1 = FTDI Basic Programmer

nets:
  GND: U1.GND, C3.-, C3.+, MOD-WIFI-ESP8266-DEV1.GND, MOD-WIFI-ESP8266-DEV1.GPIO16, MOD-WIFI-ESP8266-DEV1.GPIO15, MOD-WIFI-ESP8266-DEV1.GPIO2, ULN1.9, Composant1.GND
  N1: U1.Output, MOD-WIFI-ESP8266-DEV1.3.3V, R13.Pin_0
  N2: U1.Input_voltage, MOD-WIFI-ESP8266-DEV1.GPIO4, R2.Pin_1, R8.Pin_1, R13.Pin_1, R14.Pin_1
  N3: MOD-WIFI-ESP8266-DEV1.GPIO3, Composant1.TXO
  N4: MOD-WIFI-ESP8266-DEV1.GPIO12, ULN1.6
  N5: MOD-WIFI-ESP8266-DEV1.GPIO14, ULN1.2
  N6: MOD-WIFI-ESP8266-DEV1.GPIO13, ULN1.8
  N7: ULN1.11, LED2.cathode
  N8: ULN1.13, LED4.cathode
  N9: ULN1.17, LED3.cathode
  N10: LED2.anode, R8.Pin_0
  N11: LED3.anode, R14.Pin_0
  N12: LED4.anode, R2.Pin_0
  N13: R12.Pin_1, Composant1.RXI

notes:
  +5V Power source
  +3.3V
  GPIO 4 is the default configGPIO and set to +3.3v to enter in config mode

custom parts:
  Voltage Regulator - 3.3V: 3.3V DC Voltage Regulator
  Olimex ESP8266 DEV: MOD-WIFI-ESP8266-DEV is the ultimate development board for ESP8266 with all GPIOs and resources exposed, can be soldered to PCB or used with breadboard and UEXT. Small U.FL connector is provided for external antenna connection. ESP8266 is very highly integrated SOC which includes Xtensa LX106 core processor, RAM, RF front end and allow WIFI TCP-IP stack to be implemented on board with just few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
  2.7k Ω Resistor: A generic resistor (0.25W)
